// Logisim project Circuitos-M2.circ as structural Verilog
module Encoder_8_bits (
  output out_1,
  output out_2,
  output out_3,
  output out_4
);

  wire L_out, N_out, Ne_out, No_out, O_out, S_out, Se_out, So_out;

  Button No (.out(No_out));
  Button O (.out(O_out));
  Button So (.out(So_out));
  Button N (.out(N_out));
  Button Ne (.out(Ne_out));
  Button L (.out(L_out));
  Button Se (.out(Se_out));
  Button S (.out(S_out));
  or or_1 (out_2, No_out, O_out, So_out, S_out);
  or or_2 (out_3, No_out, O_out, Se_out, L_out);
  ExactlyOne xor_1 (
    .out(out_1), .in0(N_out), .in1(Ne_out), .in2(L_out), .in3(Se_out), .in4(S_out), .in5(So_out),
    .in6(O_out), .in7(No_out));
  or or_3 (out_4, No_out, So_out, Se_out, Ne_out);
endmodule

module Multiplexer (
  input  [15:0] in_1,
  input  [15:0] in_2,
  input  [15:0] in_3,
  input  [15:0] in_4,
  input  [15:0] in_5,
  input  [15:0] in_6,
  input  [15:0] in_7,
  input  [15:0] in_8,
  input  [2:0] in_9,
  output [18:0] out_10
);

  wire and_1_out, and_2_out, and_3_out, and_4_out, and_5_out, and_6_out, and_7_out, and_8_out, not_1_out,
       not_2_out, not_3_out, not_4_out, not_5_out, not_6_out, not_7_out, not_8_out, not_9_out, not_10_out,
       not_11_out, not_12_out;

  not not_1 (not_1_out, in_9[2]);
  assign out_10[15:0] = and_2_out ? in_1 : 16'bz;  // Controlled_Buffer controlled_buffer_1
  assign out_10[15:0] = and_1_out ? in_2 : 16'bz;  // Controlled_Buffer controlled_buffer_2
  and and_1 (and_1_out, not_6_out, not_5_out, in_9[0]);
  and and_2 (and_2_out, not_1_out, not_4_out, not_2_out);
  not not_2 (not_2_out, in_9[0]);
  not not_3 (not_3_out, in_9[2]);
  not not_4 (not_4_out, in_9[1]);
  not not_5 (not_5_out, in_9[1]);
  not not_6 (not_6_out, in_9[2]);
  assign out_10[15:0] = and_3_out ? in_3 : 16'bz;  // Controlled_Buffer controlled_buffer_3
  assign out_10[15:0] = and_4_out ? in_4 : 16'bz;  // Controlled_Buffer controlled_buffer_4
  and and_3 (and_3_out, not_3_out, in_9[1], not_7_out);
  and and_4 (and_4_out, not_8_out, in_9[1], in_9[0]);
  not not_7 (not_7_out, in_9[0]);
  not not_8 (not_8_out, in_9[2]);
  assign out_10[15:0] = and_6_out ? in_5 : 16'bz;  // Controlled_Buffer controlled_buffer_5
  assign out_10[15:0] = and_5_out ? in_6 : 16'bz;  // Controlled_Buffer controlled_buffer_6
  and and_5 (and_5_out, in_9[2], not_9_out, in_9[0]);
  and and_6 (and_6_out, in_9[2], not_10_out, not_11_out);
  not not_9 (not_9_out, in_9[1]);
  not not_10 (not_10_out, in_9[1]);
  not not_11 (not_11_out, in_9[0]);
  assign out_10[15:0] = and_7_out ? in_7 : 16'bz;  // Controlled_Buffer controlled_buffer_7
  assign out_10[15:0] = and_8_out ? in_8 : 16'bz;  // Controlled_Buffer controlled_buffer_8
  and and_7 (and_7_out, in_9[2], in_9[1], not_12_out);
  and and_8 (and_8_out, in_9[2], in_9[1], in_9[0]);
  not not_12 (not_12_out, in_9[0]);

  assign out_10[18:16] = in_9;
endmodule

module Demux (
  input  [18:0] in_1,
  output [15:0] out_2,
  output [15:0] out_3,
  output [15:0] out_4,
  output [15:0] out_5,
  output [15:0] out_6,
  output [15:0] out_7,
  output [15:0] out_8,
  output [15:0] out_9
);

  wire and_1_out, and_2_out, and_3_out, and_4_out, and_5_out, and_6_out, and_7_out, and_8_out, not_1_out,
       not_2_out, not_3_out, not_4_out, not_5_out, not_6_out, not_7_out, not_8_out, not_9_out, not_10_out,
       not_11_out, not_12_out;

  assign out_2 = and_1_out ? in_1[15:0] : 16'bz;  // Controlled_Buffer controlled_buffer_1
  assign out_3 = and_2_out ? in_1[15:0] : 16'bz;  // Controlled_Buffer controlled_buffer_2
  and and_1 (and_1_out, not_4_out, not_1_out, not_2_out);
  and and_2 (and_2_out, not_5_out, not_3_out, in_1[16]);
  not not_1 (not_1_out, in_1[17]);
  not not_2 (not_2_out, in_1[16]);
  not not_3 (not_3_out, in_1[17]);
  not not_4 (not_4_out, in_1[18]);
  not not_5 (not_5_out, in_1[18]);
  assign out_4 = and_4_out ? in_1[15:0] : 16'bz;  // Controlled_Buffer controlled_buffer_3
  assign out_5 = and_3_out ? in_1[15:0] : 16'bz;  // Controlled_Buffer controlled_buffer_4
  and and_3 (and_3_out, not_6_out, in_1[17], in_1[16]);
  and and_4 (and_4_out, not_8_out, in_1[17], not_7_out);
  not not_6 (not_6_out, in_1[18]);
  not not_7 (not_7_out, in_1[16]);
  not not_8 (not_8_out, in_1[18]);
  assign out_6 = and_6_out ? in_1[15:0] : 16'bz;  // Controlled_Buffer controlled_buffer_5
  assign out_7 = and_5_out ? in_1[15:0] : 16'bz;  // Controlled_Buffer controlled_buffer_6
  and and_5 (and_5_out, in_1[18], not_10_out, in_1[16]);
  and and_6 (and_6_out, in_1[18], not_11_out, not_9_out);
  not not_9 (not_9_out, in_1[16]);
  not not_10 (not_10_out, in_1[17]);
  not not_11 (not_11_out, in_1[17]);
  assign out_8 = and_7_out ? in_1[15:0] : 16'bz;  // Controlled_Buffer controlled_buffer_7
  assign out_9 = and_8_out ? in_1[15:0] : 16'bz;  // Controlled_Buffer controlled_buffer_8
  and and_7 (and_7_out, in_1[18], in_1[17], not_12_out);
  and and_8 (and_8_out, in_1[18], in_1[17], in_1[16]);
  not not_12 (not_12_out, in_1[16]);
endmodule

module multiplexer_do_logsim (
  input  [7:0] in_1,
  input  [7:0] in_2,
  input  [7:0] in_3,
  input  [7:0] in_4,
  input  [7:0] in_5,
  input  [7:0] in_6,
  input  [7:0] in_7,
  input  [7:0] in_8,
  input  [2:0] in_9,
  output [7:0] out_10,
  output [7:0] out_11,
  output [7:0] out_12,
  output [7:0] out_13,
  output [7:0] out_14,
  output [7:0] out_15,
  output [7:0] out_16,
  output [7:0] out_17
);

  wire [7:0] multiplexer_1_out;

  Multiplexer_part #(.select(3), .width(8)) multiplexer_1 (
    .in0(in_1), .in1(in_2), .in2(in_3), .in3(in_4), .in4(in_5), .in5(in_6), .in6(in_7), .in7(in_8),
    .out(multiplexer_1_out), .sel(in_9));  // open: en
  Demultiplexer #(.select(3), .width(8)) demultiplexer_1 (
    .out0(out_10), .out1(out_11), .out2(out_12), .out3(out_13), .out4(out_14), .out5(out_15), .out6(out_16),
    .out7(out_17), .in(multiplexer_1_out), .sel(in_9));  // open: en

  // Notes on the sheet:
  //   Ver foto dia 02/05/2017 - 21:30
endmodule

module Multiplexador (
  input  [15:0] in_1,
  input  [15:0] in_2,
  input  [15:0] in_3,
  input  [15:0] in_4,
  input  [15:0] in_5,
  input  [15:0] in_6,
  input  [15:0] in_7,
  input  [15:0] in_8,
  input  [2:0] in_9,
  output [15:0] out_10,
  output [15:0] out_11,
  output [15:0] out_12,
  output [15:0] out_13,
  output [15:0] out_14,
  output [15:0] out_15,
  output [15:0] out_16,
  output [15:0] out_17
);

  wire [18:0] multiplexer_1_out_10;

  Multiplexer multiplexer_1 (
    .in_1(in_1), .in_2(in_2), .in_3(in_3), .in_4(in_4), .in_5(in_5), .in_6(in_6), .in_7(in_7), .in_8(in_8),
    .in_9(in_9), .out_10(multiplexer_1_out_10));
  Demux demux_1 (
    .in_1(multiplexer_1_out_10), .out_2(out_10), .out_3(out_11), .out_4(out_12), .out_5(out_13),
    .out_6(out_14), .out_7(out_15), .out_8(out_16), .out_9(out_17));
endmodule

module Joystick (
  output [7:0] Coordernada_X,
  output [1:0] out_2,
  output [7:0] Coordernada_Y,
  output [1:0] out_4
);

  wire and_1_out, and_2_out, and_3_out, and_4_out, clock_1_out, clock_2_out, controlled_buffer_1_out,
       controlled_buffer_2_out, controlled_buffer_3_out, controlled_buffer_4_out, not_1_out, not_2_out,
       or_1_out, or_2_out;

  Joystick_part #(.bits(2)) joystick_1 (.x(out_2), .y(out_4));
  not not_1 (not_1_out, out_4[1]);
  not not_2 (not_2_out, out_2[1]);
  Clock clock_1 (.out(clock_1_out));
  and and_1 (and_1_out, out_2[0], out_2[1]);
  and and_2 (and_2_out, out_2[0], not_2_out);
  Clock clock_2 (.out(clock_2_out));
  and and_3 (and_3_out, out_4[0], out_4[1]);
  and and_4 (and_4_out, out_4[0], not_1_out);
  assign controlled_buffer_1_out = and_2_out ? clock_1_out : 1'bz;  // Controlled_Buffer controlled_buffer_1
  assign controlled_buffer_2_out = or_1_out ? clock_1_out : 1'bz;  // Controlled_Buffer controlled_buffer_2
  or or_1 (or_1_out, and_1_out, and_2_out);
  assign controlled_buffer_3_out = and_4_out ? clock_2_out : 1'bz;  // Controlled_Buffer controlled_buffer_3
  assign controlled_buffer_4_out = or_2_out ? clock_2_out : 1'bz;  // Controlled_Buffer controlled_buffer_4
  or or_2 (or_2_out, and_3_out, and_4_out);
  Counter #(.max('ha)) counter_1 (
    .load(controlled_buffer_1_out), .D(Coordernada_X), .count(controlled_buffer_2_out), .Q(Coordernada_X),
    .clk(controlled_buffer_2_out));  // open: carry, clr
  Counter #(.max('ha)) counter_2 (
    .load(controlled_buffer_3_out), .D(Coordernada_Y), .count(controlled_buffer_4_out), .Q(Coordernada_Y),
    .clk(controlled_buffer_4_out));  // open: carry, clr
endmodule
