// Logisim project Circuitos-M3.circ as structural Verilog
module \Laço_Dependente  (
);

  wire and_1_out, button_1_out, clock_1_out, comparator_1_lt, comparator_2_eq, or_1_out;
  wire [3:0] counter_1_q, counter_2_q;

  Counter #(.width(4), .max('h9)) counter_1 (
    .Q(counter_1_q), .clk(clock_1_out), .clr(and_1_out));  // open: load, D, count, carry
  Clock clock_1 (.out(clock_1_out));
  Button button_1 (.out(button_1_out));
  Comparator #(.width(4), .mode("unsigned")) comparator_1 (
    .a(counter_2_q), .b(counter_1_q), .lt(comparator_1_lt));  // open: gt, eq
  Counter #(.width(4), .max('h9)) counter_2 (
    .Q(counter_2_q), .clk(and_1_out), .clr(or_1_out));  // open: load, D, count, carry
  and and_1 (and_1_out, comparator_1_lt, clock_1_out);
  or or_1 (or_1_out, button_1_out, comparator_2_eq);
  Comparator #(.width(4)) comparator_2 (.a(counter_2_q), .b(4'b0111), .eq(comparator_2_eq));  // open: gt, lt
endmodule

module \Memória  (
  input  _0_Write___1___Load,
  input  Clear,
  output [7:0] out_3
);

  wire clock_1_out, controlled_buffer_1_out, counter_1_carry, not_1_out, not_2_out;
  wire [3:0] counter_1_q;
  wire [7:0] controlled_buffer_2_out, random_1_out;

  Random random_1 (.clk(controlled_buffer_1_out), .out(random_1_out));  // open: next, clr
  Counter #(.width(4), .max('hf)) counter_1 (
    .Q(counter_1_q), .carry(counter_1_carry), .clk(controlled_buffer_1_out));  // open: load, D, count, clr
  not not_1 (not_1_out, counter_1_carry);
  Clock clock_1 (.out(clock_1_out));
  assign controlled_buffer_1_out = not_1_out ? clock_1_out : 1'bz;  // Controlled_Buffer controlled_buffer_1
  assign controlled_buffer_2_out = not_2_out ? random_1_out : 8'bz;  // Controlled_Buffer controlled_buffer_2
  RAM #(.addrWidth(4)) ram_1 (
    .addr(counter_1_q), .data(controlled_buffer_2_out), .clk(controlled_buffer_1_out),
    .ld(_0_Write___1___Load), .clr(Clear));  // open: sel
  not not_2 (not_2_out, _0_Write___1___Load);
  assign out_3 = _0_Write___1___Load ? controlled_buffer_2_out : 8'bz;  // Controlled_Buffer controlled_buffer_3
endmodule

module Truco (
);

  \Memória  \memória_1  ();  // open: _0_Write___1___Load, Clear, out_3
endmodule
